# Fritzing sketch StationMeteo (saved by Fritzing 0.9.3b)
breadboards: 1

parts:
  M1 = BMP280
  Composant1 = LCD1602-I2C
  YwRobot_Power_Supply1 = YwRobot Breadboard Power Supply [part_number=545043]  # not connected
  U1 = ESP8266 ESP-01 Upgraded WiFi Module [part_number=ESP8266]

nets:
  VIN: M1.VIN, U1.VCC, U1.CH_PD
  GND: M1.GND, Composant1.GND, U1.GND
  N1: M1.SCL, Composant1.SCL, U1.GPIO_2
  N2: M1.SDA, Composant1.SDA, U1.GPIO_0

notes:
  En jaune: partie SDA de la connexion i2c
  En orange: partie SCL de la connexion i2c

custom parts:
  BMP280: Temperature Humidity Barometric presure Sensor, I2C
  LCD1602-I2C: A standard character display, usually with 2x16 characters. Comes in many colors with LCM1602 IIC attached.
  YwRobot Breadboard Power Supply: The YwRobot Breadboard Power Supply (MB-V2) has two power rails; they can be 5V or 3V3. Power to the module can be provided through the female USB socket or through the A10 (female) 2.1mm power jack.
  ESP8266 ESP-01 Upgraded WiFi Module: Upgraded Version ESP-01,all Flash are upgraded to 1M byte.Also support Cloud service remote transmission.
